# Fritzing sketch LED+Button (saved by Fritzing 1.0.5)
breadboards: 1

parts:
  Teensy1 = Teensy 3.0  # not connected
  LED1 = smd LED [color="Red (633nm)" package="0805 [SMD]"]  # not connected
  R1 = Resistor [tolerance=±5% resistance=470 package="0402 [SMD]"]  # not connected
  S1 = Momentary Switch [package=tactile-pth]
  S2 = Momentary Switch [package=tactile-pth]
  S3 = Momentary Switch [package=tactile-pth]

nets:
  N1: S1.3, S2.3, S3.3
